// Logisim project 4-Bit Comparator.circ as structural Verilog: 1 circuit, main circuit main
module main (
  input  [3:0] a,
  input  [3:0] b,
  output out_3,
  output out_4,
  output out_5
);

  wire and_1_out, and_2_out, and_3_out, and_4_out, and_5_out, and_6_out, and_7_out, and_8_out, and_9_out,
       and_10_out, and_11_out, and_12_out, and_13_out, and_14_out, nor_1_out, nor_2_out, nor_3_out,
       nor_4_out, not_1_out, not_2_out, not_3_out, not_4_out, not_5_out, not_6_out, not_7_out, not_8_out;

  not not_1 (not_1_out, a[3]);
  not not_2 (not_2_out, b[3]);
  not not_3 (not_3_out, a[2]);
  not not_4 (not_4_out, b[2]);
  not not_5 (not_5_out, a[1]);
  not not_6 (not_6_out, b[1]);
  not not_7 (not_7_out, a[0]);
  not not_8 (not_8_out, b[0]);
  and and_1 (and_1_out, not_1_out, b[3]);
  and and_2 (and_2_out, a[3], not_2_out);
  and and_3 (and_3_out, not_3_out, b[2]);
  and and_4 (and_4_out, a[2], not_4_out);
  and and_5 (and_5_out, not_5_out, b[1]);
  and and_6 (and_6_out, a[1], not_6_out);
  and and_7 (and_7_out, not_7_out, b[0]);
  and and_8 (and_8_out, a[0], not_8_out);
  nor nor_1 (nor_1_out, and_1_out, and_2_out);
  nor nor_2 (nor_2_out, and_3_out, and_4_out);
  nor nor_3 (nor_3_out, and_5_out, and_6_out);
  nor nor_4 (nor_4_out, and_7_out, and_8_out);
  and and_9 (and_9_out, nor_1_out, and_3_out);
  and and_10 (and_10_out, nor_1_out, and_4_out);
  and and_11 (and_11_out, nor_1_out, nor_2_out, and_5_out);
  and and_12 (and_12_out, nor_1_out, nor_2_out, and_6_out);
  and and_13 (and_13_out, nor_1_out, nor_2_out, nor_3_out, and_7_out);
  and and_14 (and_14_out, nor_1_out, nor_2_out, nor_3_out, and_8_out);
  and and_15 (out_5, nor_1_out, nor_2_out, nor_3_out, nor_4_out);
  or or_1 (out_3, and_1_out, and_9_out, and_11_out, and_13_out);
  or or_2 (out_4, and_2_out, and_10_out, and_12_out, and_14_out);

  // Notes on the sheet:
  //   B3
  //   A2
  //   B2
  //   A1
  //   B1
  //   A0
  //   B0
  //   A3
  //   A<B
  //   A > B
  //   A=B
endmodule
