// Logisim project CAU1B.circ as structural Verilog: 1 circuit, main circuit main
module main (
  input  [3:0] a,
  input  [3:0] b,
  input  [3:0] a_2,
  input  [3:0] b_2,
  output out_5,
  output out_6,
  output out_7,
  output [2:0] out_8,
  output [3:0] out_9
);

  wire and_1_out, and_2_out, and_3_out, and_4_out, and_5_out, and_6_out, and_7_out, and_8_out, and_9_out,
       and_10_out, and_11_out, and_12_out, and_13_out, and_14_out, and_15_out, and_16_out, and_17_out,
       and_18_out, and_19_out, and_20_out, and_21_out, and_22_out, and_24_out, and_25_out, and_26_out,
       and_27_out, and_28_out, and_29_out, nor_1_out, nor_2_out, nor_3_out, nor_4_out, nor_5_out, nor_6_out,
       nor_7_out, nor_8_out, not_1_out, not_2_out, not_3_out, not_4_out, not_5_out, not_6_out, not_7_out,
       not_8_out, not_9_out, not_10_out, not_11_out, not_12_out, not_13_out, not_14_out, not_15_out,
       not_16_out;
  wire [3:0] adder_1_out, subtractor_1_out, subtractor_2_out;

  not not_1 (not_1_out, a[3]);
  not not_2 (not_2_out, b[3]);
  not not_3 (not_3_out, a[2]);
  not not_4 (not_4_out, b[2]);
  not not_5 (not_5_out, a[1]);
  not not_6 (not_6_out, b[1]);
  not not_7 (not_7_out, a[0]);
  not not_8 (not_8_out, b[0]);
  not not_9 (not_9_out, a_2[3]);
  not not_10 (not_10_out, b_2[3]);
  not not_11 (not_11_out, a_2[2]);
  not not_12 (not_12_out, b_2[2]);
  not not_13 (not_13_out, a_2[1]);
  not not_14 (not_14_out, b_2[1]);
  not not_15 (not_15_out, a_2[0]);
  not not_16 (not_16_out, b_2[0]);
  and and_1 (and_1_out, not_1_out, b[3]);
  and and_2 (and_2_out, a[3], not_2_out);
  and and_3 (and_3_out, not_3_out, b[2]);
  and and_4 (and_4_out, a[2], not_4_out);
  and and_5 (and_5_out, not_5_out, b[1]);
  and and_6 (and_6_out, a[1], not_6_out);
  and and_7 (and_7_out, not_7_out, b[0]);
  and and_8 (and_8_out, a[0], not_8_out);
  and and_9 (and_9_out, not_9_out, b_2[3]);
  and and_10 (and_10_out, a_2[3], not_10_out);
  and and_11 (and_11_out, not_11_out, b_2[2]);
  and and_12 (and_12_out, a_2[2], not_12_out);
  and and_13 (and_13_out, not_13_out, b_2[1]);
  and and_14 (and_14_out, a_2[1], not_14_out);
  and and_15 (and_15_out, not_15_out, b_2[0]);
  and and_16 (and_16_out, a_2[0], not_16_out);
  nor nor_1 (nor_1_out, and_9_out, and_10_out);
  nor nor_2 (nor_2_out, and_11_out, and_12_out);
  nor nor_3 (nor_3_out, and_13_out, and_14_out);
  nor nor_4 (nor_4_out, and_15_out, and_16_out);
  nor nor_5 (nor_5_out, and_1_out, and_2_out);
  nor nor_6 (nor_6_out, and_3_out, and_4_out);
  nor nor_7 (nor_7_out, and_5_out, and_6_out);
  nor nor_8 (nor_8_out, and_7_out, and_8_out);
  and and_17 (and_17_out, nor_1_out, and_11_out);
  and and_18 (and_18_out, nor_1_out, and_12_out);
  and and_19 (and_19_out, nor_1_out, nor_2_out, and_13_out);
  and and_20 (and_20_out, nor_1_out, nor_2_out, and_14_out);
  and and_21 (and_21_out, nor_1_out, nor_2_out, nor_3_out, and_15_out);
  and and_22 (and_22_out, nor_1_out, nor_2_out, nor_3_out, and_16_out);
  and and_23 (out_8[2], nor_1_out, nor_2_out, nor_3_out, nor_4_out);
  and and_24 (and_24_out, nor_5_out, and_3_out);
  and and_25 (and_25_out, nor_5_out, and_4_out);
  and and_26 (and_26_out, nor_5_out, nor_6_out, and_5_out);
  and and_27 (and_27_out, nor_5_out, nor_6_out, and_6_out);
  and and_28 (and_28_out, nor_5_out, nor_6_out, nor_7_out, and_7_out);
  and and_29 (and_29_out, nor_5_out, nor_6_out, nor_7_out, and_8_out);
  and and_30 (out_7, nor_5_out, nor_6_out, nor_7_out, nor_8_out);
  or or_1 (out_5, and_1_out, and_24_out, and_26_out, and_28_out);
  or or_2 (out_6, and_2_out, and_25_out, and_27_out, and_29_out);
  or or_3 (out_8[0], and_9_out, and_17_out, and_19_out, and_21_out);
  or or_4 (out_8[1], and_10_out, and_18_out, and_20_out, and_22_out);
  Subtractor #(.width(4)) subtractor_1 (.a(b_2), .b(a_2), .out(subtractor_1_out));  // open: bin, bout
  Subtractor #(.width(4)) subtractor_2 (.a(a_2), .b(b_2), .out(subtractor_2_out));  // open: bin, bout
  Adder #(.width(4)) adder_1 (.a(a_2), .b(b_2), .out(adder_1_out));  // open: cin, cout
  Multiplexer #(.select(3), .width(4), .enable("false")) multiplexer_1 (
    .in1(subtractor_1_out), .in2(subtractor_2_out), .in4(adder_1_out), .out(out_9), .sel(out_8));  // open: in0, in3, in5, in6, in7

  // Notes on the sheet:
  //   B3
  //   A2
  //   B2
  //   A1
  //   B1
  //   A0
  //   B0
  //   A3
  //   B3
  //   A2
  //   B2
  //   A1
  //   B1
  //   A0
  //   B0
  //   A3
  //   A<B
  //   A<B
  //   A > B
  //   A=B
  //   B-A
  //   A-B
  //   A+B
  //   A > B
  //   A=B
endmodule
